# Fritzing sketch Piano (saved by Fritzing 0.9.2b)
breadboards: 2

parts:
  U1 = 74HC595 [package="DIP16 [THT]"]
  Bauteil2 = Arduino Nano (Rev3.0) (ICSP)
  U2 = 74HC595 [package="DIP16 [THT]"]
  S1 = Pushbutton [package="[SMD]"]
  S2 = Pushbutton [package="[SMD]"]
  S3 = Pushbutton [package="[SMD]"]
  S4 = Pushbutton [package="[SMD]"]
  S5 = Pushbutton [package="[SMD]"]
  S6 = Pushbutton [package="[SMD]"]
  S7 = Pushbutton [package="[SMD]"]
  S8 = Pushbutton [package="[SMD]"]
  R1 = Resistor [tolerance=±5% resistance=680 package=THT]
  R2 = Resistor [tolerance=±5% resistance=680 package=THT]
  R3 = Resistor [tolerance=±5% resistance=470 package=THT]
  R4 = Resistor [tolerance=±5% resistance=470 package=THT]
  R5 = Resistor [tolerance=±5% resistance=680 package=THT]
  R6 = Resistor [tolerance=±5% resistance=680 package=THT]
  R7 = Resistor [tolerance=±5% resistance=470 package=THT]
  R8 = Resistor [tolerance=±5% resistance=470 package=THT]
  LED1 = LED - 5mm [color="Red (633nm)" package="5 mm [THT]"]
  LED2 = LED - 5mm [color="Green (555nm)" package="5 mm [THT]"]
  LED3 = LED - 5mm [color="Blue (430nm)" package="5 mm [THT]"]
  LED4 = LED - 5mm [color="White (6500K)" package="5 mm [THT]"]
  LED5 = LED - 5mm [color="Red (633nm)" package="5 mm [THT]"]
  LED6 = LED - 5mm [color="Green (555nm)" package="5 mm [THT]"]
  LED7 = LED - 5mm [color="Blue (430nm)" package="5 mm [THT]"]
  LED8 = LED - 5mm [color="White (6500K)" package="5 mm [THT]"]
  SP1 = SPEAKER [package=pcb_mount_speaker]
  S9 = Pushbutton [package="[SMD]"]

nets:
  N1: U1.Q1, Bauteil2.D7
  N2: U1.Q2, Bauteil2.D6
  N3: U1.Q3, S5.Pin_1, S5.Pin_2
  N4: U1.Q4, S6.Pin_1, S6.Pin_2
  N5: U1.Q5, S8.Pin_1, S8.Pin_2
  N6: U1.Q6, S7.Pin_1, S7.Pin_2
  GND: U1.GND, U1.Q0, Bauteil2.GND, U2.GND, S1.Pin_3, S1.Pin_4, S2.Pin_3, S2.Pin_4, S3.Pin_3, S3.Pin_4, S4.Pin_3, S4.Pin_4, S5.Pin_3, S5.Pin_4, S6.Pin_3, S6.Pin_4, S7.Pin_3, S7.Pin_4, S8.Pin_3, S8.Pin_4, R1.Pin_0, R2.Pin_0, R3.Pin_0, R4.Pin_0, R5.Pin_0, R6.Pin_0, R7.Pin_0, R8.Pin_0, SP1.+
  N7: U1.Q7', Bauteil2.D5
  N8: U1.SH_CP, S1.Pin_1, S1.Pin_2
  N9: U1.ST_CP, S2.Pin_1, S2.Pin_2
  N10: U1.OE, S3.Pin_1, S3.Pin_2
  N11: U1.DS, S4.Pin_1, S4.Pin_2
  VCC: U1.VCC, Bauteil2.5V, U2.MR, U2.VCC
  N12: Bauteil2.D2, SP1.-
  N13: Bauteil2.D9, U2.ST_CP
  N14: Bauteil2.D10, U2.DS
  N15: Bauteil2.D11/MOSI, U2.SH_CP
  N16: U2.Q1, LED2.anode
  N17: U2.Q2, LED3.anode
  N18: U2.Q3, LED4.anode
  N19: U2.Q4, LED5.anode
  N20: U2.Q5, LED6.anode
  N21: U2.Q6, LED7.anode
  N22: U2.Q7, LED8.anode
  N23: U2.Q0, LED1.anode
  N24: R1.Pin_1, LED1.cathode
  N25: R2.Pin_1, LED2.cathode
  N26: R3.Pin_1, LED3.cathode
  N27: R4.Pin_1, LED4.cathode
  N28: R5.Pin_1, LED5.cathode
  N29: R6.Pin_1, LED6.cathode
  N30: R7.Pin_1, LED7.cathode
  N31: R8.Pin_1, LED8.cathode
  N32: S9.Pin_1, S9.Pin_2
  N33: S9.Pin_3, S9.Pin_4

notes:
  This 74* IC is a 74HC165 (multiple inputs)
